# Fritzing sketch project (saved by Fritzing 0.9.10b)
breadboards: 1

parts:
  LED1 = smd LED [color="Orange (620nm)" package="0805 [SMD]"]
  LED2 = smd LED [color="Orange (620nm)" package="0805 [SMD]"]
  LED3 = smd LED [color="Orange (620nm)" package="0805 [SMD]"]
  LED4 = smd LED [color="Orange (620nm)" package="0805 [SMD]"]
  R1 = Resistor [tolerance=±5% resistance=220 package="0603 [SMD]"]
  R2 = Resistor [tolerance=±5% resistance=220 package="0603 [SMD]"]
  R3 = Resistor [tolerance=±5% resistance=220 package="0603 [SMD]"]
  R4 = Resistor [tolerance=±5% resistance=220 package="0603 [SMD]"]
  Raspberry_Pi_3 = Raspberry Pi 3 [part_number=RPI-3-V1.2]

nets:
  N1: LED1.cathode, LED2.cathode, LED3.cathode, LED4.cathode, Raspberry_Pi_3.GND
  N2: LED1.anode, R1.Pin_1
  N3: LED2.anode, R2.Pin_0
  N4: LED3.anode, R4.Pin_0
  N5: LED4.anode, R3.Pin_1
  N6: R1.Pin_0, Raspberry_Pi_3.GPIO11
  N7: R2.Pin_1, Raspberry_Pi_3.GPIO12
  N8: R3.Pin_0, Raspberry_Pi_3.GPIO18
  N9: R4.Pin_1, Raspberry_Pi_3.GPIO21
